# Fritzing sketch iot-starter-tutorial (saved by Fritzing 0.9.3b)
breadboards: 1

parts:
  U1 = NodeMCU V1.0
  Resistor = Resistor [tolerance=±5% resistance=10k package="1206 [SMD]"]
  Photoresistor = PHOTOCELL [package=photocell]
  Resistor_2 = Resistor [tolerance=±5% resistance=330 package="1206 [SMD]"]
  Button = Square Pushbutton
  LED = LED - 3mm [color="Red (633nm)" package="3 mm [THT]"]

nets:
  N1: U1.D2, Button.leg0
  N2: U1.3V3, Photoresistor.P$1
  N3: U1.GND, Resistor.Pin_1, Resistor_2.Pin_0, Button.leg1
  N4: U1.D8, LED.anode
  N5: U1.A0, Resistor.Pin_0, Photoresistor.P$2
  N6: Resistor_2.Pin_1, LED.cathode

custom parts:
  NodeMCU V1.0: ESP8266 based NodeMCU
